# Fritzing sketch ESP8266_D1_Sensors (saved by Fritzing 0.9.10b)

parts:
  WeMos_D1_Mini1 = WeMos D1 Mini
  Part1 = Barometric Pressure Sensor - BMP180 Breakout (GY-68)

nets:
  3V3: WeMos_D1_Mini1.3V3, Part1.VCC
  N1: WeMos_D1_Mini1.D1, Part1.SCL
  N2: WeMos_D1_Mini1.D2, Part1.SDA
  N3: WeMos_D1_Mini1.G, Part1.GND
